// Logisim project CPU_Design.circ as structural Verilog: 24 circuits, main circuit main
module main (
  input  Start,
  input  Reset,
  output [9:0] out_3,
  output [3:0] out_4
);

  wire Alu_signal, and_1_out, and_2_out, CF_output, Clock, comp_sig, comparator_18_bit_1_cf,
       comparator_18_bit_1_zf, control_unit_1_is_imm, control_unit_1_jump_enable,
       control_unit_1_memread_enable, control_unit_1_memwrite_enable, control_unit_1_reg1_enable,
       control_unit_1_reg2_enable, control_unit_1_reg3_enable, Decode_signal, Fetch_signal, Load_signal,
       or_1_out, Write_F_signal, Write_RF_signal, Write_signal, ZF_output;
  wire [1:0] control_unit_1_selectbits;
  wire [3:0] control_unit_1_r1_addr, control_unit_1_r2_addr, control_unit_1_r3_addr;
  wire [5:0] control_unit_1_imm;
  wire [9:0] control_unit_1_jumpvalue, control_unit_1_mem_address;
  wire [17:0] alu_1_output, control_unit_1_memdata_store, control_unit_1_r2_out, control_unit_1_r3_out,
       control_unit_1_result, register_18_bit_1_output, register_18_bit_2_output, register_18_bit_3_output,
       register_18_bit_4_output, register_file_1_output_1, register_file_1_output_2,
       register_file_1_output_3, rom_1_data;

  Register_File register_file_1 (
    .\İnput (control_unit_1_result), .Reset(Reset), .Write_Address(control_unit_1_r1_addr),
    .Write_Enable(Write_RF_signal), .Read_Enable2(control_unit_1_reg2_enable),
    .Read_Address2(control_unit_1_r2_addr), .Read_Enable1(control_unit_1_reg1_enable),
    .Read_Address1(control_unit_1_r1_addr), .Output_1(register_file_1_output_1),
    .Output_2(register_file_1_output_2), .CLK(Clock), .Read_Enable3(control_unit_1_reg3_enable),
    .Read_Address3(control_unit_1_r3_addr), .Output_3(register_file_1_output_3));
  ROM #(.addrWidth(10), .dataWidth(18)) rom_1 (.addr(out_3), .data(rom_1_data), .sel(1'b1));
  Register_18_Bit register_18_bit_1 (
    .Input(rom_1_data), .Load(Fetch_signal), .Reset(Reset), .Clock(Clock), .Output(register_18_bit_1_output));
  Program_Counter Program_Counter (
    .JumpValue(control_unit_1_jumpvalue), .\ıncrement (Decode_signal),
    .JUMP_Enable(control_unit_1_jump_enable), .PC_out(out_3), .Reset(Reset), .Clock(Clock));
  Comparator_18_Bit comparator_18_bit_1 (
    .A(register_file_1_output_1), .B(register_file_1_output_2), .CF(comparator_18_bit_1_cf),
    .ZF(comparator_18_bit_1_zf), .Enable(comp_sig), .Reset(Reset), .Clock(Clock));
  Register_1_Bit ZF (
    .Load(Write_F_signal), .Reset(Reset), .Clock(Clock), .Input(comparator_18_bit_1_zf), .Output(ZF_output));
  Register_1_Bit CF (
    .Load(Write_F_signal), .Reset(Reset), .Clock(Clock), .Input(comparator_18_bit_1_cf), .Output(CF_output));
  Control_Unit control_unit_1 (
    .Input(register_18_bit_1_output), .clock(Clock), .ZF(ZF_output), .CF(CF_output),
    .R3(register_file_1_output_3), .R2(register_file_1_output_2), .ALU_Result(register_18_bit_4_output),
    .memdata_load(register_18_bit_2_output), .Reg1_Enable(control_unit_1_reg1_enable),
    .Reg2_Enable(control_unit_1_reg2_enable), .JUMP_Enable(control_unit_1_jump_enable),
    .Memread_Enable(control_unit_1_memread_enable), .Memwrite_Enable(control_unit_1_memwrite_enable),
    .R3_Addr(control_unit_1_r3_addr), .R2_Addr(control_unit_1_r2_addr), .R1_Addr(control_unit_1_r1_addr),
    .is_imm(control_unit_1_is_imm), .imm(control_unit_1_imm), .R2_out(control_unit_1_r2_out),
    .R3_out(control_unit_1_r3_out), .selectbits(control_unit_1_selectbits),
    .mem_address(control_unit_1_mem_address), .Reg3_Enable(control_unit_1_reg3_enable),
    .Result(control_unit_1_result), .R1(register_file_1_output_1), .JumpValue(control_unit_1_jumpvalue),
    .Start(Start), .Reset(Reset), .State(out_4), .Fetch_Signal(Fetch_signal), .Add_Signal(Alu_signal),
    .Compare_Signal(comp_sig), .memdata_store(control_unit_1_memdata_store), .Read_Signal(Load_signal),
    .Decode_Signal(Decode_signal), .R1_WRITE(Write_RF_signal), .FLAG_WRITE(Write_F_signal),
    .Write_signl_Signal(Write_signal));
  Clock clock_1 (.out(Clock));
  and and_1 (and_1_out, Load_signal, control_unit_1_memread_enable);
  and and_2 (and_2_out, Write_signal, control_unit_1_memwrite_enable);
  or or_1 (or_1_out, and_1_out, and_2_out);
  Register_18_Bit register_18_bit_2 (
    .Input(register_18_bit_3_output), .Load(Load_signal), .Reset(Reset), .Clock(Clock),
    .Output(register_18_bit_2_output));
  Register_18_Bit register_18_bit_3 (
    .Input(control_unit_1_memdata_store), .Load(control_unit_1_memwrite_enable), .Reset(Reset),
    .Clock(Clock), .Output(register_18_bit_3_output));
  ALU alu_1 (
    .imm(control_unit_1_imm), .Op1(control_unit_1_r2_out), .Op2(control_unit_1_r3_out),
    .is_immediate(control_unit_1_is_imm), .inst_bits(control_unit_1_selectbits), .Alu_enable(Alu_signal),
    .\output (alu_1_output));
  RAM #(.addrWidth(10), .dataWidth(18)) ram_1 (
    .addr(control_unit_1_mem_address), .data(register_18_bit_3_output), .sel(or_1_out), .clk(Clock),
    .ld(and_1_out));  // open: clr
  Register_18_Bit register_18_bit_4 (
    .Input(alu_1_output), .Load(Alu_signal), .Reset(Reset), .Clock(Clock), .Output(register_18_bit_4_output));

  // Notes on the sheet:
  //   Instruction Memory
  //   contents of rom_1 (hex, n*v repeats v):
  //   20000 20401 20800 20c00 21002 cd00 28050 804 4040 4480 4cc1 3ff90 2440b
  //   İNCREMENT STATE E GÖRE
  //   Data Memory
endmodule

module Negator (
  input  [17:0] in_1,
  output [17:0] out_2
);

  wire [17:0] not_18_out;

  not not_1 (not_18_out[12], in_1[12]);
  not not_2 (not_18_out[15], in_1[15]);
  not not_3 (not_18_out[17], in_1[17]);
  not not_4 (not_18_out[16], in_1[16]);
  not not_5 (not_18_out[11], in_1[11]);
  not not_6 (not_18_out[13], in_1[13]);
  not not_7 (not_18_out[14], in_1[14]);
  not not_8 (not_18_out[3], in_1[3]);
  not not_9 (not_18_out[10], in_1[10]);
  not not_10 (not_18_out[5], in_1[5]);
  not not_11 (not_18_out[7], in_1[7]);
  not not_12 (not_18_out[4], in_1[4]);
  not not_13 (not_18_out[8], in_1[8]);
  not not_14 (not_18_out[6], in_1[6]);
  not not_15 (not_18_out[9], in_1[9]);
  not not_16 (not_18_out[1], in_1[1]);
  not not_17 (not_18_out[2], in_1[2]);
  not not_18 (not_18_out[0], in_1[0]);
  Adder_18_Bit adder_18_bit_1 (.a(not_18_out), .b(18'h1), .out_4(out_2));  // open: out_3
endmodule

// Comparator
module Comparator_18_Bit (
  input  [17:0] A,
  input  [17:0] B,
  input  Enable,
  input  Reset,
  input  Clock,
  output CF,
  output ZF
);

  wire nor_1_out;
  wire [17:0] adder_18_bit_1_out_4, negator_1_out_2;

  Negator negator_1 (.in_1(B), .out_2(negator_1_out_2));
  Adder_18_Bit adder_18_bit_1 (.a(A), .b(negator_1_out_2), .out_4(adder_18_bit_1_out_4));  // open: out_3
  Register_1_Bit register_1_bit_1 (
    .Load(Enable), .Reset(Reset), .Clock(Clock), .Input(adder_18_bit_1_out_4[17]), .Output(CF));
  nor nor_1 (nor_1_out, adder_18_bit_1_out_4[17], adder_18_bit_1_out_4[16], adder_18_bit_1_out_4[15], adder_18_bit_1_out_4[14], adder_18_bit_1_out_4[13], adder_18_bit_1_out_4[12], adder_18_bit_1_out_4[11], adder_18_bit_1_out_4[10], adder_18_bit_1_out_4[9], adder_18_bit_1_out_4[8], adder_18_bit_1_out_4[7], adder_18_bit_1_out_4[6], adder_18_bit_1_out_4[5], adder_18_bit_1_out_4[4], adder_18_bit_1_out_4[3], adder_18_bit_1_out_4[2], adder_18_bit_1_out_4[1], adder_18_bit_1_out_4[0]);
  Register_1_Bit register_1_bit_2 (.Load(Enable), .Reset(Reset), .Clock(Clock), .Input(nor_1_out), .Output(ZF));
endmodule

module ALU (
  input  [5:0] imm,
  input  [17:0] Op1,
  input  [17:0] Op2,
  input  is_immediate,
  input  [1:0] inst_bits,
  input  Alu_enable,
  output [17:0] \output 
);

  wire [17:0] adder_18_bit_1_out_4, and_1_out, multiplexer_1_out, nand_1_out, nor_1_out,
       sign_extender_1_out_2;

  Sign_Extender sign_extender_1 (.in_1(imm), .out_2(sign_extender_1_out_2));
  Multiplexer #(.width(18)) multiplexer_1 (
    .in0(Op2), .in1(sign_extender_1_out_2), .out(multiplexer_1_out), .sel(is_immediate), .en(1'b1));
  Adder_18_Bit adder_18_bit_1 (.a(Op1), .b(multiplexer_1_out), .out_4(adder_18_bit_1_out_4));  // open: out_3
  assign nor_1_out = ~(Op1 | Op2);  // NOR_Gate nor_1, 18 bits wide
  assign and_1_out = Op1 & multiplexer_1_out;  // AND_Gate and_1, 18 bits wide
  assign nand_1_out = ~(Op1 & Op2);  // NAND_Gate nand_1, 18 bits wide
  Multiplexer #(.select(2), .width(18)) multiplexer_2 (
    .in0(adder_18_bit_1_out_4), .in1(nor_1_out), .in2(and_1_out), .in3(nand_1_out), .out(\output ),
    .sel(inst_bits), .en(Alu_enable));
endmodule

module Adder (
  input  ci,
  input  a,
  input  b,
  output s,
  output co
);

  wire and_1_out, and_2_out, and_3_out, xor_1_out;

  xor xor_1 (xor_1_out, b, a);
  and and_1 (and_1_out, b, a);
  and and_2 (and_2_out, b, ci);
  and and_3 (and_3_out, a, ci);
  xor xor_2 (s, xor_1_out, ci);
  or or_1 (co, and_1_out, and_2_out, and_3_out);
endmodule

module HalfAdder (
  input  a,
  input  b,
  output s,
  output co
);

  xor xor_1 (s, b, a);
  and and_1 (co, b, a);
endmodule

// Adderx2
module Adder_2_Bit (
  input  ci,
  input  [1:0] a,
  input  [1:0] b,
  output [1:0] sum,
  output co
);

  wire adder_1_co;

  Adder adder_1 (.ci(ci), .a(a[0]), .b(b[0]), .s(sum[0]), .co(adder_1_co));
  Adder adder_2 (.ci(adder_1_co), .a(a[1]), .b(b[1]), .s(sum[1]), .co(co));
endmodule

// Adderx10
module Adder_10_Bit (
  input  [9:0] a,
  input  [9:0] b,
  output out_3,
  output [9:0] out_4
);

  wire adder_2_bit_2_co, adder_2_bit_3_co, adder_2_bit_4_co, adder_2_bit_5_co;

  Adder_2_Bit adder_2_bit_1 (.ci(adder_2_bit_2_co), .a(a[9:8]), .b(b[9:8]), .sum(out_4[9:8]), .co(out_3));
  Adder_2_Bit adder_2_bit_2 (.ci(adder_2_bit_3_co), .a(a[7:6]), .b(b[7:6]), .sum(out_4[7:6]), .co(adder_2_bit_2_co));
  Adder_2_Bit adder_2_bit_3 (.ci(adder_2_bit_4_co), .a(a[5:4]), .b(b[5:4]), .sum(out_4[5:4]), .co(adder_2_bit_3_co));
  Adder_2_Bit adder_2_bit_4 (.ci(adder_2_bit_5_co), .a(a[3:2]), .b(b[3:2]), .sum(out_4[3:2]), .co(adder_2_bit_4_co));
  Adder_2_Bit adder_2_bit_5 (.ci(1'b0), .a(a[1:0]), .b(b[1:0]), .sum(out_4[1:0]), .co(adder_2_bit_5_co));
endmodule

// Adderx18
module Adder_18_Bit (
  input  [17:0] a,
  input  [17:0] b,
  output out_3,
  output [17:0] out_4
);

  wire adder_2_bit_1_co, adder_2_bit_3_co, adder_2_bit_4_co, adder_2_bit_5_co, adder_2_bit_6_co,
       adder_2_bit_7_co, adder_2_bit_8_co, adder_2_bit_9_co;

  Adder_2_Bit adder_2_bit_1 (
    .ci(adder_2_bit_3_co), .a(a[15:14]), .b(b[15:14]), .sum(out_4[15:14]), .co(adder_2_bit_1_co));
  Adder_2_Bit adder_2_bit_2 (.ci(adder_2_bit_1_co), .a(a[17:16]), .b(b[17:16]), .sum(out_4[17:16]), .co(out_3));
  Adder_2_Bit adder_2_bit_3 (
    .ci(adder_2_bit_4_co), .a(a[13:12]), .b(b[13:12]), .sum(out_4[13:12]), .co(adder_2_bit_3_co));
  Adder_2_Bit adder_2_bit_4 (
    .ci(adder_2_bit_5_co), .a(a[11:10]), .b(b[11:10]), .sum(out_4[11:10]), .co(adder_2_bit_4_co));
  Adder_2_Bit adder_2_bit_5 (.ci(adder_2_bit_6_co), .a(a[9:8]), .b(b[9:8]), .sum(out_4[9:8]), .co(adder_2_bit_5_co));
  Adder_2_Bit adder_2_bit_6 (.ci(adder_2_bit_7_co), .a(a[7:6]), .b(b[7:6]), .sum(out_4[7:6]), .co(adder_2_bit_6_co));
  Adder_2_Bit adder_2_bit_7 (.ci(adder_2_bit_8_co), .a(a[5:4]), .b(b[5:4]), .sum(out_4[5:4]), .co(adder_2_bit_7_co));
  Adder_2_Bit adder_2_bit_8 (.ci(adder_2_bit_9_co), .a(a[3:2]), .b(b[3:2]), .sum(out_4[3:2]), .co(adder_2_bit_8_co));
  Adder_2_Bit adder_2_bit_9 (.ci(1'b0), .a(a[1:0]), .b(b[1:0]), .sum(out_4[1:0]), .co(adder_2_bit_9_co));
endmodule

module D_Latch (
  input  D,
  input  C,
  output Q
);

  wire and_1_out, and_2_out, nor_1_out, not_1_out;

  not not_1 (not_1_out, D);
  and and_1 (and_1_out, D, C);
  and and_2 (and_2_out, C, not_1_out);
  nor nor_1 (nor_1_out, and_1_out, Q);
  nor nor_2 (Q, nor_1_out, and_2_out);
endmodule

module D_Flip_Flop (
  input  D,
  input  Clock,
  output Q
);

  wire d_latch_1_q, not_1_out;

  not not_1 (not_1_out, Clock);
  D_Latch d_latch_1 (.D(D), .C(not_1_out), .Q(d_latch_1_q));
  D_Latch d_latch_2 (.D(d_latch_1_q), .C(Clock), .Q(Q));
endmodule

// Regx10
module Register_10_Bit (
  input  [9:0] Input,
  input  Load,
  input  Reset,
  input  Clock,
  output [9:0] out_5
);

  Register_1_Bit register_1_bit_1 (.Load(Load), .Reset(Reset), .Clock(Clock), .Input(Input[9]), .Output(out_5[9]));
  Register_1_Bit register_1_bit_2 (.Load(Load), .Reset(Reset), .Clock(Clock), .Input(Input[8]), .Output(out_5[8]));
  Register_1_Bit register_1_bit_3 (.Load(Load), .Reset(Reset), .Clock(Clock), .Input(Input[7]), .Output(out_5[7]));
  Register_1_Bit register_1_bit_4 (.Load(Load), .Reset(Reset), .Clock(Clock), .Input(Input[6]), .Output(out_5[6]));
  Register_1_Bit register_1_bit_5 (.Load(Load), .Reset(Reset), .Clock(Clock), .Input(Input[5]), .Output(out_5[5]));
  Register_1_Bit register_1_bit_6 (.Load(Load), .Reset(Reset), .Clock(Clock), .Input(Input[4]), .Output(out_5[4]));
  Register_1_Bit register_1_bit_7 (.Load(Load), .Reset(Reset), .Clock(Clock), .Input(Input[3]), .Output(out_5[3]));
  Register_1_Bit register_1_bit_8 (.Load(Load), .Reset(Reset), .Clock(Clock), .Input(Input[2]), .Output(out_5[2]));
  Register_1_Bit register_1_bit_9 (.Load(Load), .Reset(Reset), .Clock(Clock), .Input(Input[1]), .Output(out_5[1]));
  Register_1_Bit register_1_bit_10 (.Load(Load), .Reset(Reset), .Clock(Clock), .Input(Input[0]), .Output(out_5[0]));
endmodule

// Regx18
module Register_18_Bit (
  input  [17:0] Input,
  input  Load,
  input  Reset,
  input  Clock,
  output [17:0] Output
);

  Register_1_Bit register_1_bit_1 (.Load(Load), .Reset(Reset), .Clock(Clock), .Input(Input[17]), .Output(Output[17]));
  Register_1_Bit register_1_bit_2 (.Load(Load), .Reset(Reset), .Clock(Clock), .Input(Input[16]), .Output(Output[16]));
  Register_1_Bit register_1_bit_3 (.Load(Load), .Reset(Reset), .Clock(Clock), .Input(Input[15]), .Output(Output[15]));
  Register_1_Bit register_1_bit_4 (.Load(Load), .Reset(Reset), .Clock(Clock), .Input(Input[14]), .Output(Output[14]));
  Register_1_Bit register_1_bit_5 (.Load(Load), .Reset(Reset), .Clock(Clock), .Input(Input[13]), .Output(Output[13]));
  Register_1_Bit register_1_bit_6 (.Load(Load), .Reset(Reset), .Clock(Clock), .Input(Input[12]), .Output(Output[12]));
  Register_1_Bit register_1_bit_7 (.Load(Load), .Reset(Reset), .Clock(Clock), .Input(Input[11]), .Output(Output[11]));
  Register_1_Bit register_1_bit_8 (.Load(Load), .Reset(Reset), .Clock(Clock), .Input(Input[10]), .Output(Output[10]));
  Register_1_Bit register_1_bit_9 (.Load(Load), .Reset(Reset), .Clock(Clock), .Input(Input[9]), .Output(Output[9]));
  Register_1_Bit register_1_bit_10 (.Load(Load), .Reset(Reset), .Clock(Clock), .Input(Input[8]), .Output(Output[8]));
  Register_1_Bit register_1_bit_11 (.Load(Load), .Reset(Reset), .Clock(Clock), .Input(Input[7]), .Output(Output[7]));
  Register_1_Bit register_1_bit_12 (.Load(Load), .Reset(Reset), .Clock(Clock), .Input(Input[6]), .Output(Output[6]));
  Register_1_Bit register_1_bit_13 (.Load(Load), .Reset(Reset), .Clock(Clock), .Input(Input[5]), .Output(Output[5]));
  Register_1_Bit register_1_bit_14 (.Load(Load), .Reset(Reset), .Clock(Clock), .Input(Input[4]), .Output(Output[4]));
  Register_1_Bit register_1_bit_15 (.Load(Load), .Reset(Reset), .Clock(Clock), .Input(Input[3]), .Output(Output[3]));
  Register_1_Bit register_1_bit_16 (.Load(Load), .Reset(Reset), .Clock(Clock), .Input(Input[2]), .Output(Output[2]));
  Register_1_Bit register_1_bit_17 (.Load(Load), .Reset(Reset), .Clock(Clock), .Input(Input[1]), .Output(Output[1]));
  Register_1_Bit register_1_bit_18 (.Load(Load), .Reset(Reset), .Clock(Clock), .Input(Input[0]), .Output(Output[0]));
endmodule

// Regx1
module Register_1_Bit (
  input  Input,
  input  Load,
  input  Reset,
  input  Clock,
  output Output
);

  wire and_1_out, multiplexer_1_out;

  Multiplexer multiplexer_1 (.in0(Output), .in1(Input), .out(multiplexer_1_out), .sel(Load), .en(1'b1));
  and and_1 (and_1_out, ~Reset, multiplexer_1_out);  // AND_Gate
  D_Flip_Flop d_ff_1 (.D(and_1_out), .Clock(Clock), .Q(Output));
endmodule

// RegFile
module Register_File (
  input  [17:0] \İnput ,
  input  Reset,
  input  Read_Enable3,
  input  [3:0] Read_Address3,
  input  Read_Enable2,
  input  [3:0] Read_Address2,
  input  Read_Enable1,
  input  [3:0] Write_Address,
  input  [3:0] Read_Address1,
  input  Write_Enable,
  input  CLK,
  output [17:0] Output_3,
  output [17:0] Output_2,
  output [17:0] Output_1
);

  wire and_1_out, and_2_out, and_3_out, and_4_out, and_5_out, and_6_out, and_7_out, and_8_out, and_9_out,
       and_10_out, and_11_out, and_12_out, and_13_out, and_14_out, and_15_out, and_16_out, decoder_1_out0,
       decoder_1_out1, decoder_1_out2, decoder_1_out3, decoder_1_out4, decoder_1_out5, decoder_1_out6,
       decoder_1_out7, decoder_1_out8, decoder_1_out9, decoder_1_out10, decoder_1_out11, decoder_1_out12,
       decoder_1_out13, decoder_1_out14, decoder_1_out15;
  wire [17:0] Register_1_output, Register_4_output, Register_7_output, Register_11_output,
       Register_15_output, register_18_bit_1_output, register_18_bit_2_output, register_18_bit_3_output,
       register_18_bit_4_output, register_18_bit_5_output, register_18_bit_6_output,
       register_18_bit_7_output, register_18_bit_8_output, register_18_bit_9_output,
       register_18_bit_10_output, register_18_bit_11_output;

  Decoder #(.select(4)) decoder_1 (
    .out0(decoder_1_out0), .out1(decoder_1_out1), .out2(decoder_1_out2), .out3(decoder_1_out3),
    .out4(decoder_1_out4), .out5(decoder_1_out5), .out6(decoder_1_out6), .out7(decoder_1_out7),
    .out8(decoder_1_out8), .out9(decoder_1_out9), .out10(decoder_1_out10), .out11(decoder_1_out11),
    .out12(decoder_1_out12), .out13(decoder_1_out13), .out14(decoder_1_out14), .out15(decoder_1_out15),
    .sel(Write_Address), .en(1'b1));
  and and_1 (and_1_out, decoder_1_out0, Write_Enable);
  and and_2 (and_2_out, decoder_1_out1, Write_Enable);
  and and_3 (and_3_out, decoder_1_out2, Write_Enable);
  and and_4 (and_4_out, decoder_1_out3, Write_Enable);
  and and_5 (and_5_out, decoder_1_out4, Write_Enable);
  and and_6 (and_6_out, decoder_1_out5, Write_Enable);
  and and_7 (and_7_out, decoder_1_out6, Write_Enable);
  and and_8 (and_8_out, decoder_1_out7, Write_Enable);
  and and_9 (and_9_out, decoder_1_out8, Write_Enable);
  and and_10 (and_10_out, decoder_1_out9, Write_Enable);
  and and_11 (and_11_out, decoder_1_out10, Write_Enable);
  and and_12 (and_12_out, decoder_1_out11, Write_Enable);
  and and_13 (and_13_out, decoder_1_out12, Write_Enable);
  and and_14 (and_14_out, decoder_1_out13, Write_Enable);
  and and_15 (and_15_out, decoder_1_out14, Write_Enable);
  and and_16 (and_16_out, decoder_1_out15, Write_Enable);
  Register_18_Bit Register_1 (
    .Input(\İnput ), .Load(and_1_out), .Reset(Reset), .Clock(CLK), .Output(Register_1_output));
  Register_18_Bit register_18_bit_1 (
    .Input(\İnput ), .Load(and_2_out), .Reset(Reset), .Clock(CLK), .Output(register_18_bit_1_output));
  Register_18_Bit register_18_bit_2 (
    .Input(\İnput ), .Load(and_3_out), .Reset(Reset), .Clock(CLK), .Output(register_18_bit_2_output));
  Register_18_Bit Register_4 (
    .Input(\İnput ), .Load(and_4_out), .Reset(Reset), .Clock(CLK), .Output(Register_4_output));
  Register_18_Bit register_18_bit_3 (
    .Input(\İnput ), .Load(and_5_out), .Reset(Reset), .Clock(CLK), .Output(register_18_bit_3_output));
  Register_18_Bit register_18_bit_4 (
    .Input(\İnput ), .Load(and_6_out), .Reset(Reset), .Clock(CLK), .Output(register_18_bit_4_output));
  Register_18_Bit Register_7 (
    .Input(\İnput ), .Load(and_7_out), .Reset(Reset), .Clock(CLK), .Output(Register_7_output));
  Register_18_Bit register_18_bit_5 (
    .Input(\İnput ), .Load(and_8_out), .Reset(Reset), .Clock(CLK), .Output(register_18_bit_5_output));
  Register_18_Bit register_18_bit_6 (
    .Input(\İnput ), .Load(and_9_out), .Reset(Reset), .Clock(CLK), .Output(register_18_bit_6_output));
  Register_18_Bit register_18_bit_7 (
    .Input(\İnput ), .Load(and_10_out), .Reset(Reset), .Clock(CLK), .Output(register_18_bit_7_output));
  Register_18_Bit Register_11 (
    .Input(\İnput ), .Load(and_11_out), .Reset(Reset), .Clock(CLK), .Output(Register_11_output));
  Register_18_Bit register_18_bit_8 (
    .Input(\İnput ), .Load(and_12_out), .Reset(Reset), .Clock(CLK), .Output(register_18_bit_8_output));
  Register_18_Bit register_18_bit_9 (
    .Input(\İnput ), .Load(and_13_out), .Reset(Reset), .Clock(CLK), .Output(register_18_bit_9_output));
  Register_18_Bit register_18_bit_10 (
    .Input(\İnput ), .Load(and_14_out), .Reset(Reset), .Clock(CLK), .Output(register_18_bit_10_output));
  Register_18_Bit Register_15 (
    .Input(\İnput ), .Load(and_15_out), .Reset(Reset), .Clock(CLK), .Output(Register_15_output));
  Register_18_Bit register_18_bit_11 (
    .Input(\İnput ), .Load(and_16_out), .Reset(Reset), .Clock(CLK), .Output(register_18_bit_11_output));
  Multiplexer #(.select(4), .width(18)) multiplexer_1 (
    .in0(Register_1_output), .in1(register_18_bit_1_output), .in2(register_18_bit_2_output),
    .in3(Register_4_output), .in4(register_18_bit_3_output), .in5(register_18_bit_4_output),
    .in6(Register_7_output), .in7(register_18_bit_5_output), .in8(register_18_bit_6_output),
    .in9(register_18_bit_7_output), .in10(Register_11_output), .in11(register_18_bit_8_output),
    .in12(register_18_bit_9_output), .in13(register_18_bit_10_output), .in14(Register_15_output),
    .in15(register_18_bit_11_output), .out(Output_3), .sel(Read_Address3), .en(Read_Enable3));
  Multiplexer #(.select(4), .width(18)) multiplexer_2 (
    .in0(Register_1_output), .in1(register_18_bit_1_output), .in2(register_18_bit_2_output),
    .in3(Register_4_output), .in4(register_18_bit_3_output), .in5(register_18_bit_4_output),
    .in6(Register_7_output), .in7(register_18_bit_5_output), .in8(register_18_bit_6_output),
    .in9(register_18_bit_7_output), .in10(Register_11_output), .in11(register_18_bit_8_output),
    .in12(register_18_bit_9_output), .in13(register_18_bit_10_output), .in14(Register_15_output),
    .in15(register_18_bit_11_output), .out(Output_2), .sel(Read_Address2), .en(Read_Enable2));
  Multiplexer #(.select(4), .width(18)) multiplexer_3 (
    .in0(Register_1_output), .in1(register_18_bit_1_output), .in2(register_18_bit_2_output),
    .in3(Register_4_output), .in4(register_18_bit_3_output), .in5(register_18_bit_4_output),
    .in6(Register_7_output), .in7(register_18_bit_5_output), .in8(register_18_bit_6_output),
    .in9(register_18_bit_7_output), .in10(Register_11_output), .in11(register_18_bit_8_output),
    .in12(register_18_bit_9_output), .in13(register_18_bit_10_output), .in14(Register_15_output),
    .in15(register_18_bit_11_output), .out(Output_1), .sel(Read_Address1), .en(Read_Enable1));
endmodule

// SEXT
module Sign_Extender (
  input  [5:0] in_1,
  output [17:0] out_2
);

  Multiplexer #(.width(12)) multiplexer_1 (
    .in0({12{1'b0}}), .in1({12{1'b1}}), .out(out_2[17:6]), .sel(in_1[5]), .en(1'b1));

  assign out_2[5:0] = in_1;
endmodule

module Sign_Extender_10_Bit (
  input  [5:0] in_1,
  output [9:0] out_2
);

  Multiplexer #(.width(4)) multiplexer_1 (.in0(4'b0000), .in1(4'b1111), .out(out_2[9:6]), .sel(in_1[5]), .en(1'b1));

  assign out_2[5:0] = in_1;
endmodule

// ZEXT
module Zero_Extender (
  input  [5:0] in_1,
  output [17:0] out_2
);


  assign out_2 = {{12{1'b0}}, in_1};
endmodule

module Program_Counter (
  input  Reset,
  input  Clock,
  input  [9:0] JumpValue,
  input  \ıncrement ,
  input  JUMP_Enable,
  output [9:0] PC_out
);

  wire [9:0] adder_10_bit_1_out_4, incrementer_1_out_2, register_10_bit_1_out_5;

  Register_10_Bit register_10_bit_1 (
    .Input(PC_out), .Load(1'b1), .Reset(Reset), .Clock(Clock), .out_5(register_10_bit_1_out_5));
  Incrementer incrementer_1 (.in_1(register_10_bit_1_out_5), .out_2(incrementer_1_out_2));
  Adder_10_Bit adder_10_bit_1 (
    .a(register_10_bit_1_out_5), .b(JumpValue), .out_4(adder_10_bit_1_out_4));  // open: out_3
  Multiplexer #(.select(2), .width(10), .enable("false")) multiplexer_1 (
    .in0(register_10_bit_1_out_5), .in1(incrementer_1_out_2), .in2(adder_10_bit_1_out_4), .in3({10{1'b0}}),
    .out(PC_out), .sel({JUMP_Enable, \ıncrement }));
endmodule

module Incrementer (
  input  [9:0] in_1,
  output [9:0] out_2
);

  Adder_10_Bit adder_10_bit_1 (.a(in_1), .b(10'h1), .out_4(out_2));  // open: out_3
endmodule

module OpcodeDecoder (
  input  [17:0] Instruction,
  output [3:0] Opcode,
  output [3:0] R1,
  output [3:0] R2,
  output [3:0] R3,
  output [5:0] Imm,
  output [9:0] LD_ST_Address,
  output [9:0] Jump_Address,
  output imm_bit,
  output is_LD,
  output ADD_SIGNAL,
  output NOR_SIGNAL,
  output CMP_SIGNAL,
  output AND_SIGNAL,
  output NAND_SIGNAL,
  output LD_SIGNAL,
  output ST_SIGNAL,
  output JE_SIGNAL,
  output JA_SIGNAL,
  output JB_SIGNAL,
  output JAE_SIGNAL,
  output JBE_SIGNAL,
  output JUMP_SIGNAL
);

  wire decoder_1_out0, decoder_1_out1, decoder_1_out4, decoder_1_out5;

  Decoder #(.select(4)) decoder_1 (
    .out0(decoder_1_out0), .out1(decoder_1_out1), .out2(NOR_SIGNAL), .out3(CMP_SIGNAL),
    .out4(decoder_1_out4), .out5(decoder_1_out5), .out6(NAND_SIGNAL), .out8(LD_SIGNAL), .out9(ST_SIGNAL),
    .out10(JE_SIGNAL), .out11(JA_SIGNAL), .out12(JB_SIGNAL), .out13(JAE_SIGNAL), .out14(JBE_SIGNAL),
    .out15(JUMP_SIGNAL), .sel(Instruction[17:14]), .en(1'b1));  // open: out7
  or or_1 (ADD_SIGNAL, decoder_1_out0, decoder_1_out1);
  or or_2 (AND_SIGNAL, decoder_1_out4, decoder_1_out5);

  assign Imm = Instruction[5:0];
  assign imm_bit = Instruction[14];
  assign is_LD = Instruction[17];
  assign Jump_Address = Instruction[13:4];
  assign LD_ST_Address = Instruction[9:0];
  assign Opcode = Instruction[17:14];
  assign R1 = Instruction[13:10];
  assign R2 = Instruction[9:6];
  assign R3 = Instruction[5:2];

  // Notes on the sheet:
  //   r1
  //   r2
  //   r3
  //   imm
  //   ld-st adrr
  //   addr
endmodule

module Control_Unit (
  input  [17:0] Input,
  input  ZF,
  input  CF,
  input  [17:0] R3,
  input  clock,
  input  Start,
  input  [17:0] R2,
  input  Reset,
  input  [17:0] R1,
  input  [17:0] ALU_Result,
  input  [17:0] memdata_load,
  output Reg1_Enable,
  output Reg2_Enable,
  output Reg3_Enable,
  output Memread_Enable,
  output Memwrite_Enable,
  output [9:0] JumpValue,
  output [3:0] R3_Addr,
  output [3:0] R2_Addr,
  output R1_WRITE,
  output [3:0] R1_Addr,
  output FLAG_WRITE,
  output JUMP_Enable,
  output [3:0] State,
  output is_imm,
  output [5:0] imm,
  output [17:0] R2_out,
  output [17:0] R3_out,
  output [1:0] selectbits,
  output Fetch_Signal,
  output Add_Signal,
  output Compare_Signal,
  output Read_Signal,
  output Decode_Signal,
  output Write_signl_Signal,
  output [17:0] Result,
  output [17:0] memdata_store,
  output [9:0] mem_address
);

  wire ADD, AND, COMP, is_ld, JA, JA_Enable, JAE, JAE_Enable, JB, JB_Enable, JBE, JBE_Enable, JE, JE_Enable,
       JUMP, JUMP_Enable_t, Jump_signal, NAND, NOR, or_1_out, or_2_out, or_5_out, R1_WRITE_t;
  wire [3:0] multiplexer_2_out, Opcode;

  Priority_Encoder #(.select(2)) priority_encoder_1 (
    .in0(ADD), .in1(NOR), .in2(AND), .in3(NAND), .out(selectbits));  // open: gs, en_out, en_in
  Multiplexer #(.width(18)) multiplexer_1 (.in0(ALU_Result), .in1(memdata_load), .out(Result), .sel(is_ld), .en(1'b1));
  OpcodeDecoder opcodedecoder_1 (
    .Instruction(Input), .ADD_SIGNAL(ADD), .NOR_SIGNAL(NOR), .CMP_SIGNAL(COMP), .AND_SIGNAL(AND),
    .NAND_SIGNAL(NAND), .LD_SIGNAL(Memread_Enable), .ST_SIGNAL(Memwrite_Enable), .JE_SIGNAL(JE),
    .JA_SIGNAL(JA), .JB_SIGNAL(JB), .JAE_SIGNAL(JAE), .JBE_SIGNAL(JBE), .JUMP_SIGNAL(JUMP), .R1(R1_Addr),
    .R2(R2_Addr), .R3(R3_Addr), .imm_bit(is_imm), .Imm(imm), .LD_ST_Address(mem_address),
    .Jump_Address(JumpValue), .is_LD(is_ld), .Opcode(Opcode));
  buf buffer_1 (Reg1_Enable, or_1_out);
  or or_1 (or_1_out, COMP, Memwrite_Enable);
  or or_2 (or_2_out, ADD, NOR, AND, NAND);
  or or_3 (R1_WRITE_t, ADD, NOR, NAND, AND, Memread_Enable);
  and and_1 (R1_WRITE, R1_WRITE_t, Write_signl_Signal);
  and and_2 (FLAG_WRITE, COMP, Write_signl_Signal);
  and and_3 (JUMP_Enable, Jump_signal, JUMP_Enable_t);
  or or_4 (Reg2_Enable, ADD, NOR, AND, NAND, COMP);
  and and_4 (Reg3_Enable, or_2_out, ~is_imm);  // AND_Gate
  Multiplexer #(.width(4), .enable("false")) multiplexer_2 (
    .in0(State), .in1(4'b0000), .out(multiplexer_2_out), .sel(Start));
  state state_1 (
    .opcode(Opcode), .state(multiplexer_2_out), .start(Start), .jump(JUMP_Enable_t), .Clock(clock),
    .Reset(Reset), .Next_State(State));
  or or_5 (or_5_out, ZF, CF);
  and and_5 (JE_Enable, JE, ZF, ~CF);  // AND_Gate
  and and_6 (JA_Enable, JA, ~ZF, ~CF);  // AND_Gate
  and and_7 (JB_Enable, JB, ~ZF, CF);  // AND_Gate
  and and_8 (JAE_Enable, JAE, ~CF);  // AND_Gate
  and and_9 (JBE_Enable, JBE, or_5_out);
  or or_6 (JUMP_Enable_t, JE_Enable, JA_Enable, JB_Enable, JAE_Enable, JBE_Enable, JUMP);
  and and_10 (Fetch_Signal, State[0], ~State[1], ~State[2], ~State[3]);  // AND_Gate
  and and_11 (Add_Signal, State[0], State[1], ~State[2], ~State[3]);  // AND_Gate
  and and_12 (Write_signl_Signal, ~State[0], ~State[1], ~State[2], State[3]);  // AND_Gate
  and and_13 (Compare_Signal, ~State[0], ~State[1], State[2], ~State[3]);  // AND_Gate
  and and_14 (Read_Signal, State[0], ~State[1], State[2], ~State[3]);  // AND_Gate
  and and_15 (Decode_Signal, ~State[0], State[1], ~State[2], ~State[3]);  // AND_Gate
  and and_16 (Jump_signal, State[0], State[1], State[2], ~State[3]);  // AND_Gate

  assign memdata_store = R1;
  assign R2_out = R2;
  assign R3_out = R3;

  // Other names for the same wires on the sheet: Alu_signal = Add_Signal; Carry_flag = CF; clk = clock;
  //   JUMP_Addr[9:0] = JumpValue; LD = Memread_Enable; LD_ST_Addr[9:0] = mem_address;
  //   Mem_Data_Load[17:0] = memdata_load; R1_Data[17:0] = R1; R1_t[3:0] = R1_Addr; R2_Data[17:0] = R2;
  //   R2_t[3:0] = R2_Addr; R3_Data[17:0] = R3; R3_t[3:0] = R3_Addr; REG1_READ = Reg1_Enable; REG2_READ = Reg2_Enable;
  //   REG3_READ = Reg3_Enable; ST = Memwrite_Enable; Write_signal = Write_signl_Signal; Zero_flag = ZF
endmodule

module state (
  input  [3:0] opcode,
  input  [3:0] state,
  input  Reset,
  input  start,
  input  jump,
  input  Clock,
  output [3:0] Next_State
);

  wire and_1_out, and_2_out, and_3_out, and_4_out, and_5_out, and_6_out, and_7_out, and_8_out, and_9_out,
       and_10_out, and_11_out, and_12_out, and_13_out, and_14_out, and_15_out, and_16_out, and_17_out,
       and_18_out, and_19_out, and_20_out, and_21_out, and_22_out, and_23_out, and_24_out, and_25_out,
       and_26_out, and_27_out, and_28_out, and_29_out, and_30_out, and_31_out, and_33_out, and_34_out,
       or_1_out, or_3_out, or_4_out, or_5_out, or_6_out, or_7_out, or_8_out;
  wire [3:0] not_1_out;

  and and_1 (and_1_out, ~opcode[3], ~opcode[2], opcode[1], opcode[0]);  // AND_Gate
  and and_2 (and_2_out, opcode[3], ~opcode[2], ~opcode[1], opcode[0]);  // AND_Gate
  and and_3 (and_3_out, ~state[3], state[2]);  // AND_Gate
  and and_4 (and_4_out, ~state[3], ~state[2], state[1], state[0]);  // AND_Gate
  and and_5 (and_5_out, opcode[2], opcode[1], opcode[0]);
  and and_6 (and_6_out, ~opcode[2], opcode[1], ~opcode[0]);  // AND_Gate
  and and_7 (and_7_out, ~opcode[2], opcode[1], opcode[0]);  // AND_Gate
  and and_8 (and_8_out, opcode[2], ~opcode[1], ~opcode[0]);  // AND_Gate
  and and_9 (and_9_out, opcode[2], ~opcode[1], opcode[0]);  // AND_Gate
  and and_10 (and_10_out, opcode[2], opcode[1], ~opcode[0]);  // AND_Gate
  and and_11 (and_11_out, opcode[1], ~opcode[0], jump);  // AND_Gate
  and and_12 (and_12_out, opcode[1], opcode[0], jump);
  and and_13 (and_13_out, opcode[2], ~opcode[1], opcode[0], jump);  // AND_Gate
  and and_14 (and_14_out, ~opcode[2], ~opcode[1], opcode[0]);  // AND_Gate
  and and_15 (and_15_out, opcode[2], ~opcode[1], ~opcode[0], jump);  // AND_Gate
  and and_16 (and_16_out, ~opcode[2], ~opcode[1]);  // AND_Gate
  and and_17 (and_17_out, opcode[2], ~opcode[1]);  // AND_Gate
  and and_18 (and_18_out, ~opcode[2], opcode[1], ~opcode[0]);  // AND_Gate
  and and_19 (and_19_out, opcode[2], opcode[1], ~opcode[0]);  // AND_Gate
  or or_1 (or_1_out, and_1_out, and_2_out);
  and and_20 (and_20_out, start, ~state[3], ~state[2], ~state[1], ~state[0]);  // AND_Gate
  and and_21 (and_21_out, ~state[3], ~state[2], ~state[1], state[0]);  // AND_Gate
  and and_22 (and_22_out, ~state[3], state[2], ~state[1]);  // AND_Gate
  and and_23 (and_23_out, ~state[3], state[2], state[1]);  // AND_Gate
  and and_24 (and_24_out, ~state[3], ~state[2], state[1], state[0]);  // AND_Gate
  or or_2 (not_1_out[3], and_3_out, and_4_out);
  or or_3 (or_3_out, and_16_out, and_17_out, and_18_out, and_19_out);
  and and_25 (and_25_out, ~state[3], ~state[2], state[1], ~state[0], or_1_out);  // AND_Gate
  or or_4 (or_4_out, and_5_out, and_6_out, and_7_out, and_8_out, and_9_out, and_10_out);
  or or_5 (or_5_out, and_11_out, and_12_out, and_13_out, and_14_out, and_15_out);
  and and_26 (and_26_out, or_5_out, opcode[3]);
  and and_27 (and_27_out, ~state[3], ~state[2], ~state[1], state[0]);  // AND_Gate
  and and_28 (and_28_out, or_4_out, opcode[3], jump);
  and and_29 (and_29_out, opcode[3], ~opcode[2], ~opcode[1]);  // AND_Gate
  and and_30 (and_30_out, ~opcode[3], ~opcode[2], opcode[1], opcode[0]);  // AND_Gate
  and and_31 (and_31_out, or_3_out, ~opcode[3]);  // AND_Gate
  or or_6 (or_6_out, and_25_out, and_20_out, and_21_out, and_22_out, and_23_out, and_24_out);
  or or_7 (or_7_out, and_28_out, and_29_out, and_30_out);
  or or_8 (or_8_out, and_26_out, and_31_out);
  not not_1 (not_1_out[0], or_6_out);
  and and_32 (not_1_out[2], or_7_out, and_33_out);
  and and_33 (and_33_out, ~state[3], ~state[2], state[1], ~state[0]);  // AND_Gate
  and and_34 (and_34_out, ~state[3], ~state[2], state[1], ~state[0], or_8_out);  // AND_Gate
  or or_9 (not_1_out[1], and_34_out, and_27_out);
  Register_4_bit register_4_bit_1 (.Input(not_1_out), .Load(1'b1), .Reset(Reset), .Clock(Clock), .out_5(Next_State));
endmodule

module Register_4_bit (
  input  [3:0] Input,
  input  Load,
  input  Reset,
  input  Clock,
  output [3:0] out_5
);

  Register_1_Bit register_1_bit_1 (.Load(Load), .Reset(Reset), .Clock(Clock), .Input(Input[3]), .Output(out_5[3]));
  Register_1_Bit register_1_bit_2 (.Load(Load), .Reset(Reset), .Clock(Clock), .Input(Input[2]), .Output(out_5[2]));
  Register_1_Bit register_1_bit_3 (.Load(Load), .Reset(Reset), .Clock(Clock), .Input(Input[1]), .Output(out_5[1]));
  Register_1_Bit register_1_bit_4 (.Load(Load), .Reset(Reset), .Clock(Clock), .Input(Input[0]), .Output(out_5[0]));
endmodule
